# Fritzing sketch station_meteo_LCD_RTC (saved by Fritzing 0.6.3b)
breadboards: 1

parts:
  Teensy1 = Teensy 2.0
  Y1 = Resonator [frequency="16 Mhz" package=THT]
  R1 = Resistor [tolerance=±5% resistance=4.7k package=THT]
  LCD1 = LCD screen
  R2 = Rotary Potentiometer (Small) [maximum_resistance=100kΩ]
  R3 = Rotary Potentiometer (Small) [maximum_resistance=100kΩ]
  RTC1 = DS1307_RTC_Breakout

nets:
  N1: Teensy1.GND, Y1.pin_1
  N2: Teensy1.B2, LCD1.DB7
  N3: Teensy1.B3, LCD1.DB6
  N4: Teensy1.B7, LCD1.DB5
  N5: Teensy1.D0, RTC1.connector4
  N6: Teensy1.D1, RTC1.connector3
  N7: Teensy1.C6, LCD1.DB4
  N8: Teensy1.C7, Y1.GND, R1.Pin_1
  N9: Teensy1.D6, LCD1.E
  N10: Teensy1.D7, LCD1.RS
  N11: Teensy1.VCC, Y1.0, R1.Pin_0, RTC1.connector2
  N12: LCD1.VSS, LCD1.R/W, LCD1.LED-, R2.leg1, R3.leg2, RTC1.connector1
  N13: LCD1.VDD, R2.leg2, R3.leg1
  N14: LCD1.V0, R2.wiper
  N15: LCD1.LED+, R3.wiper
