# Fritzing sketch thermal_servo_v1 (saved by Fritzing 0.6.3b)
breadboards: 1

parts:
  Arduino1 = Arduino
  IC1 = IC, DIP package, 8 pins [chip_label=IC spacing=300mil]
  LED1 = RGB LED (com. cathode, rbg) [package="5 mm [THT]"]
  J1 = Basic Servo
  J2 = Basic Servo
  Laser = LED - 5mm [color="Red (633nm)" package="5 mm [THT]"]
  S1 = Pushbutton [package=THT]
  R1 = Resistor [tolerance=±5% resistance=220 package=THT]
  R2 = Resistor [tolerance=±5% resistance=220 package=THT]
  R3 = Resistor [tolerance=±5% resistance=220 package=THT]  # not connected
  R4 = Resistor [tolerance=±5% resistance=220 package=THT]

nets:
  N1: Arduino1.D13, IC1.pin7, R1.Pin_0
  N2: Arduino1.D12, IC1.pin6, R2.Pin_0
  N3: Arduino1.D5, J2.pulse
  N4: Arduino1.D4, J1.pulse
  N5: Arduino1.3V3, IC1.pin4, LED1.blue_anode
  N6: Arduino1.+5V, IC1.pin5, S1.leg0
  N7: Arduino1.GND, IC1.pin8, LED1.green_anode, Laser.cathode, R1.Pin_1, R2.Pin_1, R4.Pin_1
  N8: IC1.pin2, LED1.common_cathode, R4.Pin_0
  N9: IC1.pin3, LED1.red_anode
  VCC: J1.vcc, J2.vcc
